# Fritzing sketch diagram (saved by Fritzing 0.8.7b)
circuit board: 8.46667cm x 5.64444cm

parts:
  U1 = ESP32S-HiLetgo [part_number=ESP32S-HiLetgo]
  Squix1 = OLED 0.96" 128x64 I2C SSD1306
  GY-NEO6MV3 = SUP500F [package=sup500f]

nets:
  VCC: U1.GPIO6, Squix1.VCC, GY-NEO6MV3.VCC
  N1: U1.GPIO7, Squix1.GND, GY-NEO6MV3.RX-I
  N2: U1.GPIO5, GY-NEO6MV3.TX-O
  N3: U1.GPIO18, GY-NEO6MV3.GND
  N4: U1.GPIO3, Squix1.SCA
  N5: U1.GPIO23, Squix1.SCL

custom parts:
  ESP32S-HiLetgo: HiLetgo ESP-WROOM-32 ESP32 ESP-32S Development Board 2.4GHz Dual-Mode WiFi + Bluetooth Dual Cores Microcontroller The ESP32 integrated with Antenna switches, RF Balun, power amplifiers, low-noise amplifiers, filters, and management modules, and the entire solution occupies the least area of PCB. 2.4 GHz Wi-Fi plus Bluetooth dual-mode chip, with TSMC Ultra-low power consumption 40nm technology,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
